# Fritzing sketch laser-tripwire (saved by Fritzing 0.8.7b)
breadboards: 1

parts:
  part = Arduino Uno (Rev3)
  LDR = Photocell (LDR) [package=THT]
  part_2 = Resistor [tolerance=±5% resistance=10k package=THT]
  Switch = Pushbutton [package=THT]
  Piezo_Buzzer = Piezo Speaker
  Laser_Diode = LD

nets:
  N1: part.A0, LDR.pin_1, part_2.Pin_1
  N2: part.D11_PWM/MOSI, Piezo_Buzzer.pin2
  N3: part.D12/MISO, Switch.leg0
  N4: part.GND, LDR.pin_0, Switch.leg1, Piezo_Buzzer.pin1, Laser_Diode.cathode
  N5: part.D3_PWM, Laser_Diode.anode
  N6: part.5V, part_2.Pin_0

custom parts:
  LD: A Generic Red Dot Laser Diode Module (~5mW)
